# Fritzing sketch BasicLed (saved by Fritzing 0.9.1b)
breadboards: 1

parts:
  LED1 = LED - 5mm [color="Red (633nm)" package="5 mm [THT]"]
  R1 = Resistor [tolerance=±5% resistance=1k package=THT]
  Part1 = Photon
  Part2 = Photon

nets:
  GND: LED1.cathode, Part1.GND, Part2.GND
  N1: LED1.anode, R1.Pin_0
  N2: R1.Pin_1, Part1.D0, Part2.D0
  N3: Part1.A0, Part2.A0
  N4: Part1.A1, Part2.A1
  N5: Part1.A2, Part2.A2
  N6: Part1.A3, Part2.A3
  N7: Part1.A4, Part2.A4
  N8: Part1.A5, Part2.A5
  N9: Part1.DAC, Part2.DAC
  N10: Part1.WKP, Part2.WKP
  N11: Part1.RX, Part2.RX
  N12: Part1.TX, Part2.TX
  VIN: Part1.VIN, Part2.VIN
  N13: Part1.D1, Part2.D1
  N14: Part1.D2, Part2.D2
  N15: Part1.D3, Part2.D3
  N16: Part1.D4, Part2.D4
  N17: Part1.D5, Part2.D5
  N18: Part1.D6, Part2.D6
  N19: Part1.D7, Part2.D7
  N20: Part1.VBAT, Part2.VBAT
  N21: Part1.RST, Part2.RST
  3V3: Part1.3V3, Part2.3V3
