# Fritzing sketch RGBLEDCircuit (saved by Fritzing 0.9.1b)
breadboards: 1

parts:
  Part1 = Photon
  S1 = Pushbutton [package="[THT]"]
  R2 = Rotary Potentiometer (Small) [maximum_resistance=10kΩ package=THT]
  LED1 = RGB LED (com. cathode, rgb) [package="5 mm [THT]"]
  LED2 = LED - 5mm [color="Red (633nm)" package="5 mm [THT]"]
  R4 = Resistor [tolerance=±5% resistance=220 package=THT]
  R6 = Resistor [tolerance=±5% resistance=10k package=THT]  # not connected
  R7 = Resistor [tolerance=±5% resistance=220 package=THT]
  R8 = Resistor [tolerance=±5% resistance=220 package=THT]

nets:
  N1: Part1.A0, R2.wiper
  N2: Part1.GND, S1.Pin_3, S1.Pin_4, R2.leg1, LED2.cathode
  N3: Part1.D0, R8.Pin_1
  N4: Part1.D1, R4.Pin_1
  N5: Part1.D2, R7.Pin_1
  N6: Part1.D3, LED2.anode
  N7: Part1.D4, S1.Pin_1, S1.Pin_2
  N8: Part1.3V3, R2.leg2, LED1.common_cathode
  N9: LED1.red_anode, R8.Pin_0
  N10: LED1.green_anode, R4.Pin_0
  N11: LED1.blue_anode, R7.Pin_0
